# Fritzing sketch BOM_10pin_syringe (saved by Fritzing 0.9.3b)
circuit board: 4.7935cm x 2.74754cm
breadboards: 1

parts:
  J440 = shrouded pin header, 10 pins [form="♂ (shrouded male)"]
  J441 = female pin header, 3 pins [form="♀ (female)"]
  J442 = female pin header, 4 pins [form="♀ (female)"]
  J443 = female pin header, 3 pins [form="♀ (female)"]

nets:
  N1: J440.pin1, J442.pin4
  N2: J440.pin2, J442.pin3
  N3: J440.pin3, J442.pin2
  N4: J440.pin4, J442.pin1
  N5: J440.pin5, J441.pin1
  N6: J440.pin6, J441.pin2
  N7: J440.pin7, J441.pin3
  N8: J440.pin8, J443.pin3
  N9: J440.pin9, J443.pin2
  N10: J440.pin10, J443.pin1
