# Fritzing sketch BOM_amplifier_brd_holder (saved by Fritzing 0.9.3b)
circuit board: 6.22991cm x 9.15281cm
breadboards: 1

parts:
  J548 = female pin header, 10 pins [form="♀ (female)"]
  R45 = Resistor [tolerance=±5% resistance=10k package=THT]
  J549 = female pin header, 3 pins [form="♀ (female)"]
  J550 = female pin header, 3 pins [form="♀ (female)"]
  J551 = female pin header, 3 pins [form="♀ (female)"]
  J552 = female pin header, 3 pins [form="♀ (female)"]
  J553 = female pin header, 4 pins [form="♀ (female)"]
  Part15 = Arduino Micro (Rev3)
  J554 = shrouded pin header, 10 pins [form="♂ (shrouded male)"]
  J555 = female pin header, 3 pins [form="♀ (female)"]
  J556 = female pin header, 3 pins [form="♀ (female)"]
  J557 = female pin header, 3 pins [form="♀ (female)"]

nets:
  N1: J548.pin1, R45.Pin_0, Part15.MISO
  N2: J548.pin2, J549.pin3, J550.pin3, J551.pin3, J552.pin3, Part15.A0
  N3: J548.pin3, Part15.D5_PWM
  N4: J548.pin4, Part15.D6_PWM/A7
  N5: J548.pin7, J551.pin1, J553.pin4
  N6: J548.pin8, J552.pin1, J553.pin3
  N7: J548.pin9, J550.pin1, J553.pin2
  N8: J548.pin10, J549.pin1, J553.pin1
  N9: R45.Pin_1, J549.pin2, J550.pin2, J551.pin2, J552.pin2
  N10: J554.pin1, J557.pin1
  N11: J554.pin2, J557.pin2
  N12: J554.pin3, J557.pin3
  N13: J554.pin4, J556.pin1
  N14: J554.pin5, J556.pin2
  N15: J554.pin7, J555.pin3
  N16: J554.pin8, J555.pin2
  N17: J554.pin9, J555.pin1
  N18: J554.pin10, J556.pin3
