# Fritzing sketch BOM_atxpowerconnect (saved by Fritzing 0.9.3b)
circuit board: 9.89535cm x 9.94463cm
breadboards: 1

parts:
  J666 = ATX24 Pin Power Supply Connector [package=atx24_right_angle]
  J667 = female pin header, 1 pin [form="♀ (female)"]
  J668 = female pin header, 1 pin [form="♀ (female)"]
  J669 = female pin header, 1 pin [form="♀ (female)"]
  J670 = female pin header, 1 pin [form="♀ (female)"]
  J671 = female pin header, 1 pin [form="♀ (female)"]
  J672 = female pin header, 1 pin [form="♀ (female)"]
  J673 = female pin header, 1 pin [form="♀ (female)"]
  J674 = female pin header, 1 pin [form="♀ (female)"]
  F17 = FUSE [package=fuse_5mm]
  F18 = FUSE [package=fuse_5mm]
  F19 = FUSE [package=fuse_5mm]
  F20 = FUSE [package=fuse_5mm]
  F21 = FUSE [package=fuse_5mm]
  F22 = FUSE [package=fuse_5mm]
  F23 = FUSE [package=fuse_5mm]
  F24 = FUSE [package=fuse_5mm]
  J676 = screw terminal, 2 pins
  J677 = screw terminal, 2 pins
  J678 = screw terminal, 2 pins
  J679 = screw terminal, 2 pins
  J680 = screw terminal, 2 pins
  J681 = screw terminal, 2 pins
  J682 = screw terminal, 2 pins
  R47 = Resistor [tolerance=±5% resistance=220 package=THT]
  LED10 = LED - 5mm [color="Red (633nm)" package="5 mm [THT]"]
  Pad3 = Pad [width=6 height=6 connect=center]  # not connected
  Pad4 = Pad [width=6 height=6 connect=center]  # not connected
  J675 = screw terminal, 2 pins

nets:
  N1: J666.3.3V, F19.1
  N2: J666.GND, J666.PS_ON, J667.pin1, J668.pin1, J670.pin1, J671.pin1, J676.pin2, J677.pin2, J678.pin2, J679.pin2, J680.pin2, J681.pin2, J682.pin2, LED10.anode, J675.pin2
  N3: J666.5V, F18.1, F21.1, F23.1, R47.Pin_1
  N4: J666.12V, J669.pin1, J672.pin1, J673.pin1, J674.pin1, F17.1, F20.1, F22.1, F24.1
  N5: F17.2, J676.pin1
  N6: F18.2, J682.pin1
  N7: F19.2, J675.pin1
  N8: F20.2, J679.pin1
  N9: F21.2, J678.pin1
  N10: F22.2, J681.pin1
  N11: F23.2, J680.pin1
  N12: F24.2, J677.pin1
  N13: R47.Pin_0, LED10.cathode

notes:
  HTS ATX POWER
  - +
  3.3V
  5V
  12 V
