# Fritzing sketch BOM_conveyer_pcb (saved by Fritzing 0.9.3b)
circuit board: 12.1215cm x 9.62049cm
breadboards: 1

parts:
  J594 = screw terminal, 2 pins
  J595 = female pin header, 8 pins [form="♀ (female)"]  # not connected
  J596 = female pin header, 8 pins [form="♀ (female)"]  # not connected
  J597 = female pin header, 8 pins [form="♀ (female)"]
  J598 = female pin header, 8 pins [form="♀ (female)"]
  J599 = female pin header, 8 pins [form="♀ (female)"]
  J600 = female pin header, 8 pins [form="♀ (female)"]
  J601 = female pin header, 8 pins [form="♀ (female)"]
  J602 = female pin header, 8 pins [form="♀ (female)"]
  J603 = female pin header, 8 pins [form="♀ (female)"]
  J604 = female pin header, 8 pins [form="♀ (female)"]
  J605 = female pin header, 4 pins [form="♀ (female)"]
  J606 = female pin header, 4 pins [form="♀ (female)"]
  J607 = female pin header, 4 pins [form="♀ (female)"]
  J608 = female pin header, 4 pins [form="♀ (female)"]
  J609 = female pin header, 4 pins [form="♀ (female)"]
  J610 = female pin header, 3 pins [form="♀ (female)"]
  J611 = female pin header, 9 pins [form="♀ (female)"]
  J612 = female pin header, 6 pins [form="♀ (female)"]
  J613 = female pin header, 6 pins [form="♀ (female)"]
  J614 = female pin header, 5 pins [form="♀ (female)"]
  J615 = female pin header, 6 pins [form="♀ (female)"]
  J616 = female pin header, 12 pins [form="♀ (female)"]
  Part15 = Arduino Micro (Rev3)
  MD09B22 = A4988 Stepper Motor Driver Carrier
  MD09B23 = A4988 Stepper Motor Driver Carrier
  MD09B24 = A4988 Stepper Motor Driver Carrier
  MD09B25 = A4988 Stepper Motor Driver Carrier
  MD09B26 = A4988 Stepper Motor Driver Carrier
  J617 = female pin header, 2 pins [form="♀ (female)"]
  J618 = female pin header, 2 pins [form="♀ (female)"]
  J619 = female pin header, 2 pins [form="♀ (female)"]
  J620 = female pin header, 2 pins [form="♀ (female)"]
  J621 = female pin header, 3 pins [form="♀ (female)"]
  J622 = female pin header, 3 pins [form="♀ (female)"]
  J623 = female pin header, 3 pins [form="♀ (female)"]
  J624 = female pin header, 3 pins [form="♀ (female)"]
  J625 = female pin header, 1 pin [form="♀ (female)"]
  J626 = female pin header, 2 pins [form="♀ (female)"]
  J627 = female pin header, 2 pins [form="♀ (female)"]
  J628 = female pin header, 2 pins [form="♀ (female)"]
  J629 = female pin header, 2 pins [form="♀ (female)"]
  J630 = female pin header, 2 pins [form="♀ (female)"]
  J631 = female pin header, 2 pins [form="♀ (female)"]
  J632 = female pin header, 2 pins [form="♀ (female)"]
  J633 = female pin header, 2 pins [form="♀ (female)"]
  J634 = female pin header, 2 pins [form="♀ (female)"]
  J635 = female pin header, 2 pins [form="♀ (female)"]
  J636 = female pin header, 2 pins [form="♀ (female)"]
  J637 = female pin header, 2 pins [form="♀ (female)"]
  J638 = female pin header, 2 pins [form="♀ (female)"]
  J639 = female pin header, 2 pins [form="♀ (female)"]
  J640 = female pin header, 2 pins [form="♀ (female)"]
  J641 = female pin header, 2 pins [form="♀ (female)"]
  J642 = female pin header, 2 pins [form="♀ (female)"]
  J643 = female pin header, 3 pins [form="♀ (female)"]
  J644 = female pin header, 3 pins [form="♀ (female)"]
  J645 = female pin header, 3 pins [form="♀ (female)"]
  J646 = female pin header, 3 pins [form="♀ (female)"]
  J647 = female pin header, 3 pins [form="♀ (female)"]
  J648 = female pin header, 5 pins [form="♀ (female)"]
  J649 = female pin header, 5 pins [form="♀ (female)"]

nets:
  N1: J594.pin1, MD09B22.VMOT, MD09B23.VMOT, MD09B24.VMOT, MD09B25.VMOT, MD09B26.VMOT, J628.pin2, J629.pin2, J630.pin2, J631.pin2, J632.pin2, J633.pin2, J634.pin2, J635.pin2, J636.pin2, J637.pin2, J638.pin2, J639.pin2, J640.pin2, J641.pin1, J642.pin1
  N2: J594.pin2, MD09B22.GROUND#141, MD09B26.GROUND#141, J628.pin1, J632.pin1, J636.pin1, J640.pin1, J641.pin2, J642.pin2
  N3: J597.pin5, MD09B22.SLEEP
  N4: J598.pin5, MD09B23.SLEEP
  N5: J599.pin5, MD09B24.SLEEP
  N6: J600.pin5, MD09B25.SLEEP
  N7: J601.pin2, MD09B25.GROUND#141, J631.pin1, J635.pin1, J639.pin1
  N8: J601.pin3, J605.pin1
  3V3: J601.pin7, J602.pin7, J603.pin7, J604.pin7, J611.pin8, J613.pin1, J613.pin2, J613.pin3, J613.pin4, J613.pin5, J613.pin6, Part15.3V3, MD09B26.MS1, MD09B26.MS2, MD09B26.MS3, MD09B26.VDD, J617.pin1, J618.pin1, J619.pin1, J620.pin1, J627.pin1, J643.pin2, J644.pin2, J645.pin2, J646.pin2, J647.pin2
  N9: J602.pin3, J606.pin1
  N10: J603.pin2, MD09B23.GROUND#141, J629.pin1, J633.pin1, J637.pin1
  N11: J603.pin3, J607.pin1
  N12: J604.pin2, MD09B24.GROUND#141, J630.pin1, J634.pin1, J638.pin1
  N13: J604.pin3, J608.pin1
  N14: J605.pin2, MD09B22.OUT_2A
  N15: J605.pin3, MD09B22.OUT_1A
  N16: J605.pin4, MD09B22.OUT_1B
  N17: J606.pin2, MD09B23.OUT_2A
  N18: J606.pin3, MD09B23.OUT_1A
  N19: J606.pin4, MD09B23.OUT_1B
  N20: J607.pin2, MD09B24.OUT_2A
  N21: J607.pin3, MD09B24.OUT_1A
  N22: J607.pin4, MD09B24.OUT_1B
  N23: J608.pin2, MD09B25.OUT_2A
  N24: J608.pin3, MD09B25.OUT_1A
  N25: J608.pin4, MD09B25.OUT_1B
  N26: J609.pin1, MD09B26.OUT_2B
  N27: J609.pin2, MD09B26.OUT_2A
  N28: J609.pin3, MD09B26.OUT_1A
  N29: J609.pin4, MD09B26.OUT_1B
  N30: J610.pin1, J616.pin6, Part15.GND, MD09B22.GROUND#147, MD09B23.GROUND#147, MD09B24.GROUND#147, MD09B25.GROUND#147, MD09B26.GROUND#147, J617.pin2, J618.pin2, J619.pin2, J620.pin2, J627.pin2, J643.pin1, J644.pin1, J645.pin1, J646.pin1, J647.pin1
  N31: J610.pin2, J616.pin5, Part15.RESET
  N32: J610.pin3, Part15.5V
  N33: J611.pin1, Part15.A5
  N34: J611.pin2, Part15.A4, J647.pin3
  N35: J611.pin3, Part15.A3, J643.pin3
  N36: J611.pin4, Part15.A2, J644.pin3
  N37: J611.pin5, Part15.A1, J646.pin3
  N38: J611.pin6, Part15.A0, J645.pin3
  N39: J611.pin7, Part15.AREF
  N40: J611.pin9, J615.pin1, J615.pin2, J615.pin3, J615.pin4, J615.pin5, J615.pin6, Part15.D13_PWM
  N41: J612.pin1, J612.pin2, J612.pin3, J612.pin4, J612.pin5, J612.pin6, J616.pin12, Part15.D7
  N42: J614.pin1, Part15.D8_PWM/A8
  N43: J614.pin2, Part15.D9_PWM/A9
  N44: J614.pin3, Part15.D10_PWM/A10
  N45: J614.pin4, Part15.D11_PWM
  N46: J614.pin5, Part15.D12_PWM/A11
  N47: J616.pin1, Part15.MOSI
  N48: J616.pin2, Part15.RXLED/SS
  N49: J616.pin3, Part15.D1/TX
  N50: J616.pin4, Part15.D0/RX
  N51: J616.pin7, Part15.D2/SDA
  N52: J616.pin8, Part15.D3/SCL
  N53: J616.pin9, Part15.D4_PWM/A6
  N54: J616.pin10, Part15.D5_PWM
  N55: J616.pin11, Part15.D6_PWM/A7
  N56: MD09B22.Enable, J621.pin3
  N57: MD09B22.MS1, MD09B22.MS2, MD09B22.MS3, MD09B22.VDD
  N58: MD09B22.STEP, J621.pin1
  N59: MD09B22.DIR, J621.pin2
  N60: MD09B23.Enable, J622.pin3
  N61: MD09B23.MS1, MD09B23.MS2, MD09B23.MS3, MD09B23.VDD
  N62: MD09B23.STEP, J622.pin1
  N63: MD09B23.DIR, J622.pin2
  N64: MD09B24.Enable, J623.pin3
  N65: MD09B24.MS1, MD09B24.MS2, MD09B24.MS3, MD09B24.VDD
  N66: MD09B24.STEP, J623.pin1
  N67: MD09B24.DIR, J623.pin2
  N68: MD09B25.Enable, J624.pin3
  N69: MD09B25.MS1, MD09B25.MS2, MD09B25.MS3, MD09B25.VDD
  N70: MD09B25.STEP, J624.pin1
  N71: MD09B25.DIR, J624.pin2
  N72: MD09B26.Enable, J625.pin1
  N73: MD09B26.RESET, MD09B26.SLEEP
  N74: MD09B26.STEP, J626.pin1
  N75: MD09B26.DIR, J626.pin2
  N76: J648.pin1, J649.pin1
  N77: J648.pin2, J649.pin2
  N78: J648.pin3, J649.pin3
  N79: J648.pin4, J649.pin4
  N80: J648.pin5, J649.pin5

notes:
  - +
  12V
  HTS Resources
  5 stepper
  endstops
  solenoid_brd connects
