# Fritzing sketch BOM_conveyer_solenoids (saved by Fritzing 0.9.3b)
circuit board: 8.29914cm x 3.94585cm
breadboards: 1

parts:
  R36 = Resistor [tolerance=±5% resistance=1k package=THT]
  R37 = Resistor [tolerance=±5% resistance=1k package=THT]
  R38 = Resistor [tolerance=±5% resistance=1k package=THT]
  R39 = Resistor [tolerance=±5% resistance=1k package=THT]
  J416 = female pin header, 1 pin [form="♀ (female)"]
  J417 = female pin header, 1 pin [form="♀ (female)"]
  J418 = female pin header, 1 pin [form="♀ (female)"]
  J419 = female pin header, 1 pin [form="♀ (female)"]
  J420 = female pin header, 1 pin [form="♀ (female)"]
  J421 = female pin header, 1 pin [form="♀ (female)"]
  J422 = female pin header, 1 pin [form="♀ (female)"]
  J423 = female pin header, 1 pin [form="♀ (female)"]
  J424 = female pin header, 1 pin [form="♀ (female)"]
  J425 = female pin header, 1 pin [form="♀ (female)"]
  J426 = female pin header, 1 pin [form="♀ (female)"]
  J427 = female pin header, 1 pin [form="♀ (female)"]
  J428 = female pin header, 2 pins [form="♀ (female)"]
  J429 = female pin header, 2 pins [form="♀ (female)"]
  J430 = female pin header, 2 pins [form="♀ (female)"]
  J431 = female pin header, 5 pins [form="♀ (female)"]
  J432 = female pin header, 2 pins [form="♀ (female)"]
  J433 = female pin header, 2 pins [form="♀ (female)"]
  J434 = female pin header, 1 pin [form="♀ (female)"]
  J435 = female pin header, 1 pin [form="♀ (female)"]
  J436 = female pin header, 1 pin [form="♀ (female)"]
  J437 = female pin header, 3 pins [form="♀ (female)"]
  J438 = female pin header, 3 pins [form="♀ (female)"]
  J439 = female pin header, 3 pins [form="♀ (female)"]
  J440 = female pin header, 3 pins [form="♀ (female)"]
  J441 = Screw terminal - 2 pins [package=THT]

nets:
  N1: R36.Pin_0, J431.pin1
  N2: R37.Pin_0, J431.pin2
  N3: R38.Pin_0, J431.pin4
  N4: R38.Pin_1, J440.pin1
  N5: R39.Pin_0, J431.pin3
  N6: J416.pin1, J427.pin1, J430.pin2, J440.pin2
  N7: J417.pin1, J419.pin1, J421.pin1, J424.pin1, J428.pin1, J431.pin5, J437.pin3, J438.pin3, J439.pin3, J440.pin3, J441.pin1
  N8: J418.pin1, J420.pin1, J432.pin2, J437.pin2
  N9: J422.pin1, J423.pin1, J433.pin2, J438.pin2
  N10: J425.pin1, J426.pin1, J429.pin2, J439.pin2
  N11: J428.pin2, J429.pin1, J430.pin1, J432.pin1, J433.pin1, J441.pin2
  N12: J434.pin1, J437.pin1
  N13: J435.pin1, J438.pin1
  N14: J436.pin1, J439.pin1
