# Fritzing sketch BOM_diaphragm_washpumps (saved by Fritzing 0.9.3b)
circuit board: 6.11275cm x 4.01882cm
breadboards: 1

parts:
  J1 = female pin header, 6 pins [form="♀ (female)"]
  J2 = female pin header, 6 pins [form="♀ (female)"]
  LED2 = LED - 5mm [color="Red (633nm)" package="5 mm [THT]"]
  R2 = Resistor [tolerance=±5% resistance=10k package=THT]
  LED3 = LED - 5mm [color="Red (633nm)" package="5 mm [THT]"]
  LED4 = LED - 5mm [color="Red (633nm)" package="5 mm [THT]"]
  LED5 = LED - 5mm [color="Red (633nm)" package="5 mm [THT]"]

nets:
  N1: J1.pin1, J2.pin1, R2.Pin_0
  N2: J1.pin2, J2.pin2, LED4.anode
  N3: J1.pin3, J2.pin3, LED3.anode
  N4: J1.pin4, J2.pin4, LED2.anode
  N5: J1.pin6, J2.pin6, LED5.anode
  N6: LED2.cathode, R2.Pin_1, LED3.cathode, LED4.cathode, LED5.cathode

notes:
  HTS Resources Pumps Board
  -
  1 2 3 12V
